# Fritzing sketch Diagrama ByteBots - Motor Driver Shield + Arduino Mega (saved by Fritzing 0.9.3b)

parts:
  Motor_Driver_Shield = AF_mshield-v1.2_breadboard
  Arduino_Mega = Arduino Mega ADK (Rev3)

nets:
  GND: Motor_Driver_Shield.GND, Arduino_Mega.GND
  N1: Motor_Driver_Shield.PWM0A, Arduino_Mega.D6_PWM
  N2: Motor_Driver_Shield.DIR_LATCH, Arduino_Mega.D12_PWM
  N3: Motor_Driver_Shield.3#89, Arduino_Mega.D2_PWM
  N4: Motor_Driver_Shield.PWM2B, Arduino_Mega.D3_PWM
  N5: Motor_Driver_Shield.DIR_CLK, Arduino_Mega.D4_PWM
  N6: Motor_Driver_Shield.PWM0B, Arduino_Mega.D5_PWM
  N7: Motor_Driver_Shield.DIR_EN, Arduino_Mega.D7_PWM
  N8: Motor_Driver_Shield.DIR_SER, Arduino_Mega.D8_PWM
  N9: Motor_Driver_Shield.PWM1A, Arduino_Mega.D9_PWM
  N10: Motor_Driver_Shield.PWM1B, Arduino_Mega.D10_PWM
  N11: Motor_Driver_Shield.PWM2A, Arduino_Mega.D11_PWM
  N12: Motor_Driver_Shield.RESET, Arduino_Mega.RESET
  VCC: Motor_Driver_Shield.VCC, Arduino_Mega.IOREF, Arduino_Mega.5V
  9V: Motor_Driver_Shield.9V, Arduino_Mega.VIN
  N13: Motor_Driver_Shield.1, Arduino_Mega.A0
  N14: Motor_Driver_Shield.2, Arduino_Mega.A1
  N15: Motor_Driver_Shield.3#111, Arduino_Mega.A2
  N16: Motor_Driver_Shield.4, Arduino_Mega.A3
  N17: Motor_Driver_Shield.5, Arduino_Mega.A4
  N18: Motor_Driver_Shield.6, Arduino_Mega.A5

custom parts:
  : motor Shield v1 Adafruit Adafruit Motor/Stepper/Servo Shield for Arduino kit [v1.2] : ID 81 : $19.50 : Adafruit Industries, Unique & fun DIY electronics and kits
