# Fritzing sketch Esquema-Bytebots (saved by Fritzing 0.9.3b)

parts:
  Componente1 = Arduino Mega ADK (Rev3)
  A1 = HuskyLens-Vision-Sensor_1
  J1 = Basic Servo
  U1 = HC-SR04 [chip_label=IC package="SIP (Single Inline) [THT]"]
  M1 = DC Motor
  Componente3 = AF_mshield-v1.2_breadboard
  M2 = fc-51 [package=THT]
  M3 = fc-51 [package=THT]
  Bat1 = battery_holder_single_18650
  Bat2 = battery_holder_single_18650

nets:
  N1: Componente1.A8, M2.pin1
  N2: Componente1.A9, M3.pin1
  N3: Componente1.D21/SCL, A1.pin2
  N4: Componente1.D20/SDA, A1.pin1
  GND: A1.pin3, J1.gnd, U1.GND, Componente3.GND, M2.pin2, M3.pin2, Bat1.+#0, Bat2.+#1
  VCC: A1.pin4, J1.vcc, U1.Vcc, Componente3.VCC, M2.pin3, M3.pin3
  N5: J1.pulse, Componente3.PWM1B
  N6: U1.Trig, Componente3.6
  N7: U1.Echo, Componente3.5
  N8: M1.pin_1, Componente3.N$31, Componente3.P2
  N9: M1.pin_2, Componente3.P1
  N10: Componente3.V+, Bat1.+#1, Bat2.+#0

custom parts:
  HuskyLens-Vision-Sensor_1: Huskylens is an easy-to-use AI Camera | Vision Sensor. DFrobot Huskylens is equipped with multiple functions, such as face recognition, object tracking, object recognition, line tracking, color recognition, and tag(QR code) recognition.
  HC-SR04: HC-SR04 ultrasound distance sensor
  : motor Shield v1 Adafruit Adafruit Motor/Stepper/Servo Shield for Arduino kit [v1.2] : ID 81 : $19.50 : Adafruit Industries, Unique & fun DIY electronics and kits
  battery_holder_single_18650: single 18650 battery holder
